# Fritzing sketch irripi (saved by Fritzing 0.9.3b)

parts:
  Raspberry_Pi1 = Raspberry Pi 2
  Composant4 = Real Time Clock Module - DS1307 RTC Breakout Board
  U4 = 4RelayModule
  LCD2004-I2C1 = LCD2004-I2C
  J1 = Power Jack [package=power_jack_pth]
  J2 = Power Jack [package=power_jack_pth]
  L1 = Solenoid  # not connected
  L4 = Solenoid  # not connected
  S1 = SPST Switch [package=switche-dpdt]
  S2 = SPST Switch [package=switche-dpdt]
  S3 = SPST Switch [package=switche-dpdt]
  S4 = SPST Switch [package=switche-dpdt]
  F1 = FUSE [part_number=0.5A package=fuse_5mm]
  L5 = Solenoid
  L6 = Solenoid  # not connected
  F2 = FUSE [part_number=0.5A package=fuse_5mm]
  F3 = FUSE [part_number=0.5A package=fuse_5mm]
  F4 = FUSE [part_number=0.5A package=fuse_5mm]

nets:
  N1: Raspberry_Pi1.GPIO2, Composant4.SDA, LCD2004-I2C1.SDA
  N2: Raspberry_Pi1.GPIO3, Composant4.SCL, LCD2004-I2C1.SCL
  N3: Raspberry_Pi1.GPIO4, U4.IN1
  N4: Raspberry_Pi1.GPIO17, U4.IN2
  N5: Raspberry_Pi1.GPIO27, U4.IN3
  N6: Raspberry_Pi1.GPIO22, U4.IN4
  GND: Raspberry_Pi1.GND, Composant4.GND, U4.GND, LCD2004-I2C1.GND, J1.GND
  5V: Raspberry_Pi1.5V, Composant4.5V, U4.VCC, LCD2004-I2C1.VCC, J1.PWR
  N7: U4.CC1, S4.S
  N8: U4.CC2, S3.S
  N9: U4.NC3, U4.NC4, J2.GND, S1.O, S2.O, S3.O, S4.O
  N10: U4.CC3, S2.S
  N11: U4.CC4, S1.S
  N12: S1.P, F4.1
  N13: S2.P, F1.1
  N14: S3.P, F2.1
  N15: S4.P, F3.1
  N16: F1.2, L5.pin2

notes:
  DS3231 i2c 5v
  2 water pressure analog sensor
  lcd 20*4 i2c
  relay for solenoid valve
  multiple by the number of solenoid valve
  5V FOR RPI
  24V AC FOR SOLENOID VALVE
  fuse 5x20 0.5A
  Switch 3 Positions For Manual Control
  Solenoid Valve Rainbird dv100
  Projet IrriPi

custom parts:
  4RelayModule: 4 relay arduino module SONGLE SRD05VDC-SL-C
  LCD2004-I2C: A standard character display with 4x20 characters. Comes in many colors with LCM2004 IIC attached.
